# Fritzing sketch iharp (saved by Fritzing 0.9.3b)
breadboards: 1

parts:
  VCC1 = 4 x AAA Battery Mount
  U1 = attiny85 [package=dip]
  R1 = Resistor [tolerance=±5% resistance=470 package=THT]
  Bauteil1 = ws2812b [package="smd 2812b"]

nets:
  N1: VCC1.-, U1.Pin_4, Bauteil1.VSS
  N2: VCC1.+, U1.Pin_8, Bauteil1.VDD
  N3: U1.Pin_3, R1.Pin_1
  N4: R1.Pin_0, Bauteil1.DIN
